# Fritzing sketch multitime (saved by Fritzing 0.9.2b)
breadboards: 2

parts:
  U1 = 74HC595 [package="DIP16 [THT]"]
  U2 = 74HC595 [package="DIP16 [THT]"]
  S1 = Pushbutton [package="[THT]"]
  R1 = Resistor [tolerance=±5% resistance=2.2k package=THT]
  Parte1 = Arduino Nano (Rev3.0)
  SPKR1 = Loudspeaker
  Q1 = NPN-Transistor [part_number=BC547 package="TO92 [THT]"]
  R2 = Resistor [tolerance=±5% resistance=47 package=THT]
  Q2 = MOSFET-NCHANNEL [part_number=2N7000 package=to-92]
  R3 = Resistor [tolerance=±5% resistance=220 package=THT]
  R4 = Resistor [tolerance=±5% resistance=220 package=THT]
  R5 = Resistor [tolerance=±5% resistance=220 package=THT]
  R6 = Resistor [tolerance=±5% resistance=220 package=THT]
  R7 = Resistor [tolerance=±5% resistance=220 package=THT]
  R8 = Resistor [tolerance=±5% resistance=220 package=THT]
  R9 = Resistor [tolerance=±5% resistance=220 package=THT]
  R10 = Resistor [tolerance=±5% resistance=220 package=THT]
  R11 = Resistor [tolerance=±5% resistance=330 package=THT]
  R12 = Resistor [tolerance=±5% resistance=330 package=THT]
  R13 = Resistor [tolerance=±5% resistance=330 package=THT]
  R14 = Resistor [tolerance=±5% resistance=330 package=THT]
  R15 = Resistor [tolerance=±5% resistance=330 package=THT]
  R16 = Resistor [tolerance=±5% resistance=330 package=THT]
  R17 = Resistor [tolerance=±5% resistance=330 package=THT]
  J1 = male pin header, 11 pins [form="♂ (male)"]
  R18 = Resistor [tolerance=±5% resistance=330 package=THT]
  R19 = Resistor [tolerance=±5% resistance=180 package=THT]
  R20 = Resistor [tolerance=±5% resistance=10k package=THT]
  J2 = male pin header, 11 pins [form="♂ (male)"]
  Q3 = MOSFET-NCHANNEL [part_number=2N7000 package=to-92]
  R21 = Resistor [tolerance=±5% resistance=180 package=THT]
  R22 = Resistor [tolerance=±5% resistance=180 package=THT]
  R23 = Resistor [tolerance=±5% resistance=180 package=THT]
  Q4 = MOSFET-NCHANNEL [part_number=2N7000 package=to-92]
  Q5 = MOSFET-NCHANNEL [part_number=2N7000 package=to-92]
  R24 = Resistor [tolerance=±5% resistance=10k package=THT]
  R25 = Resistor [tolerance=±5% resistance=10k package=THT]
  R26 = Resistor [tolerance=±5% resistance=10k package=THT]
  R27 = Resistor [tolerance=±5% resistance=180 package=THT]
  R28 = Resistor [tolerance=±5% resistance=10k package=THT]
  Q6 = MOSFET-NCHANNEL [part_number=2N7000 package=to-92]
  Q7 = MOSFET-NCHANNEL [part_number=2N7000 package=to-92]
  Q8 = MOSFET-NCHANNEL [part_number=2N7000 package=to-92]
  Q9 = MOSFET-NCHANNEL [part_number=2N7000 package=to-92]
  R29 = Resistor [tolerance=±5% resistance=180 package=THT]
  R30 = Resistor [tolerance=±5% resistance=180 package=THT]
  R31 = Resistor [tolerance=±5% resistance=180 package=THT]
  R32 = Resistor [tolerance=±5% resistance=10k package=THT]
  R33 = Resistor [tolerance=±5% resistance=10k package=THT]
  R34 = Resistor [tolerance=±5% resistance=10k package=THT]

nets:
  N1: U1.Q1, R4.Pin_1
  N2: U1.Q2, R5.Pin_1
  N3: U1.Q3, R6.Pin_1
  N4: U1.Q4, R7.Pin_1
  N5: U1.Q5, R8.Pin_0
  N6: U1.Q6, R10.Pin_0
  N7: U1.Q7, R9.Pin_0
  GND: U1.GND, U1.OE, U2.GND, U2.OE, S1.Pin_1, S1.Pin_2, Parte1.GND, Q1.E, Q2.D, R20.Pin_0, Q3.D, Q4.D, Q5.D, R24.Pin_0, R25.Pin_0, R26.Pin_0, R28.Pin_1, Q6.D, Q7.D, Q8.D, Q9.D, R32.Pin_1, R33.Pin_1, R34.Pin_1
  VCC: U1.MR, U1.VCC, U2.MR, U2.VCC, Parte1.5V, SPKR1.pin2
  N8: U1.SH_CP, U2.SH_CP, Parte1.D13/SCK
  N9: U1.ST_CP, U2.ST_CP, Parte1.D9
  N10: U1.DS, U2.Q7'
  N11: U1.Q0, R3.Pin_1
  N12: U2.Q1, R12.Pin_1
  N13: U2.Q2, R13.Pin_1
  N14: U2.Q3, R14.Pin_1
  N15: U2.Q4, R15.Pin_1
  N16: U2.Q5, R16.Pin_0
  N17: U2.Q6, R17.Pin_0
  N18: U2.Q7, R18.Pin_0
  N19: U2.DS, Parte1.D11/MOSI
  N20: U2.Q0, R11.Pin_1
  N21: S1.Pin_3, S1.Pin_4, Parte1.D2
  N22: R1.Pin_0, Parte1.D3
  N23: R1.Pin_1, Q1.B
  N24: Parte1.D4, R23.Pin_0
  N25: Parte1.D5, R22.Pin_0
  N26: Parte1.D6, R21.Pin_0
  N27: Parte1.D7, R19.Pin_0
  N28: Parte1.A3, R31.Pin_0
  N29: Parte1.A2, R30.Pin_0
  N30: Parte1.A1, R29.Pin_0
  N31: Parte1.A0, R27.Pin_0
  N32: SPKR1.pin1, R2.Pin_1
  N33: Q1.C, R2.Pin_0
  N34: Q2.S, R19.Pin_1, R20.Pin_1
  N35: Q2.G, J1.pin1
  N36: R3.Pin_0, J2.pin5
  N37: R4.Pin_0, J2.pin6
  N38: R5.Pin_0, J2.pin7
  N39: R6.Pin_0, J2.pin8
  N40: R8.Pin_1, J2.pin9
  N41: R9.Pin_1, J2.pin11
  N42: R10.Pin_1, J2.pin10
  N43: R11.Pin_0, J1.pin5
  N44: R12.Pin_0, J1.pin6
  N45: R13.Pin_0, J1.pin7
  N46: R14.Pin_0, J1.pin8
  N47: R16.Pin_1, J1.pin9
  N48: R17.Pin_1, J1.pin10
  N49: J1.pin2, Q3.G
  N50: J1.pin3, Q4.G
  N51: J1.pin4, Q5.G
  N52: J1.pin11, R18.Pin_1
  N53: J2.pin1, Q6.G
  N54: J2.pin2, Q7.G
  N55: J2.pin3, Q8.G
  N56: J2.pin4, Q9.G
  N57: Q3.S, R21.Pin_1, R24.Pin_1
  N58: R22.Pin_1, Q4.S, R26.Pin_1
  N59: R23.Pin_1, Q5.S, R25.Pin_1
  N60: R27.Pin_1, R28.Pin_0, Q6.S
  N61: Q7.S, R29.Pin_1, R32.Pin_0
  N62: Q8.S, R30.Pin_1, R33.Pin_0
  N63: Q9.S, R31.Pin_1, R34.Pin_0

notes:
  Display 8x8 bicolor common cathode
  YSM-2088CR3G2C
